// Logisim project ADDER16B.circ as structural Verilog: 14 circuits, main circuit halfadder
module halfadder (
  input  A,
  input  B,
  output S,
  output CO
);

  xor xor_1 (S, A, B);
  and and_1 (CO, A, B);
endmodule

module fulladder (
  input  Ci,
  input  A,
  input  B,
  output S,
  output CO
);

  wire halfadder_1_co, halfadder_1_s, halfadder_2_co;

  halfadder halfadder_1 (.A(A), .B(B), .S(halfadder_1_s), .CO(halfadder_1_co));
  halfadder halfadder_2 (.A(Ci), .B(halfadder_1_s), .S(S), .CO(halfadder_2_co));
  or or_1 (CO, halfadder_2_co, halfadder_1_co);
endmodule

module adder_4b_72112a86 (
  input  C0,
  input  A0,
  input  B0,
  input  A1,
  input  B1,
  input  A2,
  input  B2,
  input  A3,
  input  B3,
  output S0,
  output S1,
  output S2,
  output S3,
  output C4
);

  wire fulladder_1_co, fulladder_2_co, fulladder_3_co;

  fulladder fulladder_1 (.Ci(C0), .A(A0), .B(B0), .S(S0), .CO(fulladder_1_co));
  fulladder fulladder_2 (.Ci(fulladder_1_co), .A(A1), .B(B1), .S(S1), .CO(fulladder_2_co));
  fulladder fulladder_3 (.Ci(fulladder_2_co), .A(A2), .B(B2), .S(S2), .CO(fulladder_3_co));
  fulladder fulladder_4 (.Ci(fulladder_3_co), .A(A3), .B(B3), .S(S3), .CO(C4));
endmodule

module adder_8b_f77c325d (
  input  C0,
  input  A0,
  input  B0,
  input  A1,
  input  B1,
  input  A2,
  input  B2,
  input  A3,
  input  B3,
  input  A4,
  input  B4,
  input  A5,
  input  B5,
  input  A6,
  input  B6,
  input  A7,
  input  B7,
  output S0,
  output S1,
  output S2,
  output S3,
  output S4,
  output S5,
  output S6,
  output S7,
  output C8
);

  wire adder_4b_72112a86_1_c4;

  adder_4b_72112a86 adder_4b_72112a86_1 (
    .C0(C0), .A0(A0), .B0(B0), .A1(A1), .B1(B1), .A2(A2), .B2(B2), .A3(A3), .B3(B3), .S0(S0), .S1(S1),
    .S2(S2), .S3(S3), .C4(adder_4b_72112a86_1_c4));
  adder_4b_72112a86 adder_4b_72112a86_2 (
    .C0(adder_4b_72112a86_1_c4), .A0(A4), .B0(B4), .A1(A5), .B1(B5), .A2(A6), .B2(B6), .A3(A7), .B3(B7),
    .S0(S4), .S1(S5), .S2(S6), .S3(S7), .C4(C8));
endmodule

module ADDER_16B_83416b62 (
  input  C0,
  input  A0,
  input  B0,
  input  A1,
  input  B1,
  input  A2,
  input  B2,
  input  A3,
  input  B3,
  input  A4,
  input  B4,
  input  A5,
  input  B5,
  input  A6,
  input  B6,
  input  A7,
  input  B7,
  input  A8,
  input  B8,
  input  A9,
  input  B9,
  input  A10,
  input  B10,
  input  A11,
  input  B11,
  input  A12,
  input  B12,
  input  A13,
  input  B13,
  input  A14,
  input  B14,
  input  A15,
  input  B15,
  output S0,
  output S1,
  output S2,
  output S3,
  output S4,
  output S5,
  output S6,
  output S7,
  output S8,
  output S9,
  output S10,
  output S11,
  output S12,
  output S13,
  output S14,
  output S15,
  output C
);

  wire adder_8b_f77c325d_1_c8, displayund_1_a, displayund_1_b, displayund_1_c, displayund_1_d,
       displayund_1_e, displayund_1_f, displayund_1_g, displayund_2_a, displayund_2_b, displayund_2_c,
       displayund_2_d, displayund_2_e, displayund_2_f, displayund_2_g, displayund_3_a, displayund_3_b,
       displayund_3_c, displayund_3_d, displayund_3_e, displayund_3_f, displayund_3_g, displayund_4_a,
       displayund_4_b, displayund_4_c, displayund_4_d, displayund_4_e, displayund_4_f, displayund_4_g;

  adder_8b_f77c325d adder_8b_f77c325d_1 (
    .C0(C0), .A0(A0), .B0(B0), .A1(A1), .B1(B1), .A2(A2), .B2(B2), .A3(A3), .B3(B3), .A4(A4), .B4(B4),
    .A5(A5), .B5(B5), .A6(A6), .B6(B6), .A7(A7), .B7(B7), .S0(S0), .S1(S1), .S2(S2), .S3(S3), .S4(S4),
    .S5(S5), .S6(S6), .S7(S7), .C8(adder_8b_f77c325d_1_c8));
  adder_8b_f77c325d adder_8b_f77c325d_2 (
    .C0(adder_8b_f77c325d_1_c8), .A0(A8), .B0(B8), .A1(A9), .B1(B9), .A2(A10), .B2(B10), .A3(A11), .B3(B11),
    .A4(A12), .B4(B12), .A5(A13), .B5(B13), .A6(A14), .B6(B14), .A7(A15), .B7(B15), .S0(S8), .S1(S9),
    .S2(S10), .S3(S11), .S4(S12), .S5(S13), .S6(S14), .S7(S15), .C8(C));
  DisplayUnd displayund_1 (
    .A0(S0), .B0(S1), .A1(S2), .B1(S3), .a(displayund_1_a), .b(displayund_1_b), .c(displayund_1_c),
    .d(displayund_1_d), .e(displayund_1_e), .f(displayund_1_f), .g(displayund_1_g));
  DisplayUnd displayund_2 (
    .A0(S4), .B0(S5), .A1(S6), .B1(S7), .a(displayund_2_a), .b(displayund_2_b), .c(displayund_2_c),
    .d(displayund_2_d), .e(displayund_2_e), .f(displayund_2_f), .g(displayund_2_g));
  DisplayUnd displayund_3 (
    .A0(S8), .B0(S11), .A1(S9), .B1(S10), .a(displayund_3_a), .b(displayund_3_b), .c(displayund_3_c),
    .d(displayund_3_d), .e(displayund_3_e), .f(displayund_3_f), .g(displayund_3_g));
  DisplayUnd displayund_4 (
    .A0(S12), .B0(S13), .A1(S14), .B1(S15), .a(displayund_4_a), .b(displayund_4_b), .c(displayund_4_c),
    .d(displayund_4_d), .e(displayund_4_e), .f(displayund_4_f), .g(displayund_4_g));
  _7_Segment_Display u_7_segment_display_1 (
    .g(displayund_4_g), .f(displayund_4_f), .a(displayund_4_a), .b(displayund_4_b), .e(displayund_4_e),
    .d(displayund_4_d), .c(displayund_4_c));  // open: dp
  _7_Segment_Display u_7_segment_display_2 (
    .g(displayund_3_g), .f(displayund_3_f), .a(displayund_3_a), .b(displayund_3_b), .e(displayund_3_e),
    .d(displayund_3_d), .c(displayund_3_c));  // open: dp
  _7_Segment_Display u_7_segment_display_3 (
    .g(displayund_2_g), .f(displayund_2_f), .a(displayund_2_a), .b(displayund_2_b), .e(displayund_2_e),
    .d(displayund_2_d), .c(displayund_2_c));  // open: dp
  _7_Segment_Display u_7_segment_display_4 (
    .g(displayund_1_g), .f(displayund_1_f), .a(displayund_1_a), .b(displayund_1_b), .e(displayund_1_e),
    .d(displayund_1_d), .c(displayund_1_c));  // open: dp
endmodule

module SegB (
  input  B0,
  input  B1,
  input  B2,
  input  B3,
  output out_5
);

  wire and_1_out, and_2_out, and_3_out, and_4_out, and_5_out, not_1_out, not_2_out, not_3_out, not_4_out;

  not not_1 (not_1_out, B0);
  not not_2 (not_2_out, B1);
  not not_3 (not_3_out, B2);
  not not_4 (not_4_out, B3);
  and and_1 (and_1_out, not_4_out, not_2_out, not_1_out);
  and and_2 (and_2_out, not_4_out, B1, B0);
  and and_3 (and_3_out, not_3_out, not_1_out);
  and and_4 (and_4_out, B3, not_2_out, B0);
  and and_5 (and_5_out, not_4_out, not_3_out);
  or or_1 (out_5, and_1_out, and_2_out, and_3_out, and_4_out, and_5_out);
endmodule

module SegA (
  input  B0,
  input  B1,
  input  B2,
  input  B3,
  output A
);

  wire and_1_out, and_2_out, and_3_out, and_4_out, and_5_out, and_6_out, not_1_out, not_2_out, not_3_out,
       not_4_out, or_1_out, or_2_out, or_3_out;

  not not_1 (not_1_out, B0);
  not not_2 (not_2_out, B1);
  not not_3 (not_3_out, B2);
  not not_4 (not_4_out, B3);
  and and_1 (and_1_out, not_3_out, not_1_out);
  and and_2 (and_2_out, not_4_out, B1);
  and and_3 (and_3_out, not_4_out, B2, B0);
  and and_4 (and_4_out, B3, not_3_out, not_2_out);
  and and_5 (and_5_out, B3, not_1_out);
  and and_6 (and_6_out, B2, B1);
  or or_1 (or_1_out, and_1_out, and_2_out);
  or or_2 (or_2_out, and_3_out, and_4_out);
  or or_3 (or_3_out, and_5_out, and_6_out);
  or or_4 (A, or_1_out, or_2_out, or_3_out);
endmodule

module SegC (
  input  B0,
  input  B1,
  input  B2,
  input  B3,
  output C
);

  wire and_1_out, and_2_out, and_3_out, and_4_out, and_5_out, not_2_out, not_3_out, not_4_out;

  // NOT_Gate not_1 has open pins: in=B0, out=open
  not not_2 (not_2_out, B1);
  not not_3 (not_3_out, B2);
  not not_4 (not_4_out, B3);
  and and_1 (and_1_out, not_4_out, B2);
  and and_2 (and_2_out, B3, not_3_out);
  and and_3 (and_3_out, not_2_out, B0);
  and and_4 (and_4_out, not_3_out, not_2_out);
  and and_5 (and_5_out, not_3_out, B0);
  or or_1 (C, and_1_out, and_2_out, and_3_out, and_4_out, and_5_out);
endmodule

module SegE (
  input  B0,
  input  B1,
  input  B2,
  input  B3,
  output E
);

  wire and_1_out, and_2_out, and_3_out, and_4_out, not_1_out, not_3_out;

  not not_1 (not_1_out, B0);
  // NOT_Gate not_2 has open pins: in=B1, out=open
  not not_3 (not_3_out, B2);
  // NOT_Gate not_4 has open pins: in=B3, out=open
  and and_1 (and_1_out, not_3_out, not_1_out);
  and and_2 (and_2_out, B1, not_1_out);
  and and_3 (and_3_out, B3, B1);
  and and_4 (and_4_out, B3, B2);
  or or_1 (E, and_1_out, and_2_out, and_3_out, and_4_out);
endmodule

module SegF (
  input  B0,
  input  B1,
  input  B2,
  input  B3,
  output F
);

  wire and_1_out, and_2_out, and_3_out, and_4_out, and_5_out, not_1_out, not_2_out, not_3_out, not_4_out;

  not not_1 (not_1_out, B0);
  not not_2 (not_2_out, B1);
  not not_3 (not_3_out, B2);
  not not_4 (not_4_out, B3);
  and and_1 (and_1_out, not_2_out, not_1_out);
  and and_2 (and_2_out, not_4_out, B2, not_2_out);
  and and_3 (and_3_out, B2, not_1_out);
  and and_4 (and_4_out, B3, not_3_out);
  and and_5 (and_5_out, B3, B1);
  or or_1 (F, and_1_out, and_2_out, and_3_out, and_4_out, and_5_out);
endmodule

module SegG (
  input  B0,
  input  B1,
  input  B2,
  input  B3,
  output G
);

  wire and_1_out, and_2_out, and_3_out, and_4_out, and_5_out, not_1_out, not_2_out, not_3_out, not_4_out;

  not not_1 (not_1_out, B0);
  not not_2 (not_2_out, B1);
  not not_3 (not_3_out, B2);
  not not_4 (not_4_out, B3);
  and and_1 (and_1_out, not_3_out, B1);
  and and_2 (and_2_out, B3, not_3_out);
  and and_3 (and_3_out, not_4_out, B2, not_2_out);
  and and_4 (and_4_out, B1, not_1_out);
  and and_5 (and_5_out, B3, B0);
  or or_1 (G, and_1_out, and_2_out, and_3_out, and_4_out, and_5_out);
endmodule

module SegD (
  input  B0,
  input  B1,
  input  B2,
  input  B3,
  output D
);

  wire and_1_out, and_2_out, and_3_out, and_4_out, and_5_out, and_6_out, not_1_out, not_2_out, not_3_out,
       not_4_out;

  not not_1 (not_1_out, B0);
  not not_2 (not_2_out, B1);
  not not_3 (not_3_out, B2);
  not not_4 (not_4_out, B3);
  and and_1 (and_1_out, not_2_out, B3);
  and and_2 (and_2_out, not_1_out, B1, not_4_out);
  and and_3 (and_3_out, B0, not_2_out, B2);
  and and_4 (and_4_out, B0, B3);
  and and_5 (and_5_out, not_1_out, not_3_out, not_4_out);
  and and_6 (and_6_out, B1, not_3_out, not_4_out);
  or or_1 (D, and_1_out, and_2_out, and_3_out, and_4_out, and_5_out, and_6_out);
endmodule

module DisplayUnd (
  input  A0,
  input  B0,
  input  A1,
  input  B1,
  output a,
  output b,
  output c,
  output d,
  output e,
  output f,
  output g
);

  SegA sega_1 (.B0(A0), .B1(B0), .B2(A1), .B3(B1), .A(a));
  SegB segb_1 (.B0(A0), .B1(B0), .B2(A1), .B3(B1), .out_5(b));
  SegC segc_1 (.B0(A0), .B1(B0), .B2(A1), .B3(B1), .C(c));
  SegD2 segd2_1 (.B0(A0), .B1(B0), .B2(A1), .B3(B1), .D(d));
  SegE sege_1 (.B0(A0), .B1(B0), .B2(A1), .B3(B1), .E(e));
  SegF segf_1 (.B0(A0), .B1(B0), .B2(A1), .B3(B1), .F(f));
  SegG segg_1 (.B0(A0), .B1(B0), .B2(A1), .B3(B1), .G(g));
endmodule

module SegD2 (
  input  B0,
  input  B1,
  input  B2,
  input  B3,
  output D
);

  wire and_1_out, and_2_out, and_3_out, and_4_out, and_5_out, not_1_out, not_2_out, not_3_out, not_4_out;

  not not_1 (not_1_out, B0);
  not not_2 (not_2_out, B1);
  not not_3 (not_3_out, B2);
  not not_4 (not_4_out, B3);
  and and_1 (and_1_out, not_2_out, B3);
  and and_2 (and_2_out, not_1_out, B1, not_4_out);
  and and_3 (and_3_out, B0, not_2_out, B2);
  and and_4 (and_4_out, B0, B1, not_3_out);
  and and_5 (and_5_out, not_1_out, not_2_out, not_3_out);
  or or_1 (D, and_1_out, and_2_out, and_3_out, and_4_out, and_5_out);
endmodule
