// Logisim project questao4.circ as structural Verilog: 2 circuits, main circuit Padrao
module Padrao (
  input  H,
  input  U,
  input  T,
  input  F,
  output A
);

  wire and_1_out, and_2_out, and_3_out, and_4_out;

  and and_1 (and_1_out, H, T);
  and and_2 (and_2_out, U, F);
  and and_3 (and_3_out, U, T, F);
  and and_4 (and_4_out, U, T, H);
  or or_1 (A, and_1_out, and_2_out, and_3_out, and_4_out);

  // Notes on the sheet:
  //   A = H⋅T+U⋅F+U⋅T⋅F+U⋅T⋅H
endmodule

module Simplificado (
  input  H,
  input  U,
  input  T,
  input  F,
  output A
);

  wire and_1_out, and_2_out;

  and and_1 (and_1_out, U, F);
  and and_2 (and_2_out, H, T);
  or or_1 (A, and_1_out, and_2_out);

  // Notes on the sheet:
  //   A = U⋅F+H⋅T
endmodule
