// Logisim project Questao05.circ as structural Verilog: 1 circuit, main circuit Questao5
module Questao5 (
  input  B2,
  input  B1,
  input  B0,
  output Y3,
  output Y2,
  output Y1,
  output Y0
);

  wire and_3_out, and_4_out, and_5_out, not_1_out, not_2_out, not_3_out;

  not not_1 (not_1_out, B2);
  not not_2 (not_2_out, B1);
  not not_3 (not_3_out, B0);
  and and_1 (Y3, B2, B1);
  and and_2 (Y2, B2, not_2_out);
  and and_3 (and_3_out, not_1_out, not_2_out, not_3_out);
  and and_4 (and_4_out, B1, B0);
  and and_5 (and_5_out, B2, B0);
  or or_1 (Y1, and_3_out, and_4_out, and_5_out);

  assign Y0 = 1'b1;

  // Notes on the sheet:
  //   Y3 = B2*B1
  //   Y2 = B2*B1'
  //   Y1 = B2'*B1'*B0' + B1*B0 + B2*B0
  //   Y0 = 1
endmodule
