// Logisim project item_c.circ as structural Verilog: 1 circuit, main circuit main
module main (
  input  A,
  input  B,
  input  C,
  input  D,
  output X
);

  wire or_1_out;

  or or_1 (or_1_out, C, D);
  nand nand_1 (X, A, B, or_1_out);
endmodule
