// Logisim project SOMADOR 16 BITS.circ as structural Verilog: 1 circuit, main circuit main
module main (
  input  D,
  input  A0,
  input  B0,
  input  A1,
  input  B1,
  input  A2,
  input  B2,
  input  A3,
  input  B3,
  input  A4,
  input  B4,
  input  A5,
  input  B5,
  input  A6,
  input  B6,
  input  A7,
  input  B7,
  input  A8,
  input  B8,
  input  A9,
  input  B9,
  input  A10,
  input  B10,
  input  A11,
  input  B11,
  input  A12,
  input  B12,
  input  A13,
  input  B13,
  input  A14,
  input  B14,
  input  A15,
  input  B15,
  output S0,
  output C0,
  output S1,
  output C1,
  output S2,
  output C2,
  output S3,
  output C3,
  output S4,
  output C4,
  output S5,
  output C5,
  output S6,
  output C6,
  output S7,
  output C7,
  output S8,
  output C8,
  output S9,
  output C9,
  output S10,
  output C10,
  output S11,
  output C11,
  output S12,
  output C12,
  output S13,
  output C13,
  output S14,
  output C14,
  output S15,
  output C15
);

  wire and_1_out, and_2_out, and_3_out, and_4_out, and_5_out, and_6_out, and_7_out, and_8_out, and_9_out,
       and_10_out, and_11_out, and_12_out, and_13_out, and_14_out, and_15_out, and_16_out, and_17_out,
       and_18_out, and_19_out, and_20_out, and_21_out, and_22_out, and_23_out, and_24_out, and_25_out,
       and_26_out, and_27_out, and_28_out, and_29_out, and_30_out, and_31_out, and_32_out, and_33_out,
       and_34_out, and_35_out, and_36_out, and_37_out, and_38_out, and_39_out, and_40_out, and_41_out,
       and_42_out, and_43_out, and_44_out, and_45_out, and_46_out, and_47_out, and_48_out;

  and and_1 (and_1_out, A0, B0);
  and and_2 (and_2_out, A0, D);
  and and_3 (and_3_out, B0, D);
  ExactlyOne xor_1 (.out(S0), .in0(A0), .in1(D), .in2(B0));
  or or_1 (C0, and_1_out, and_2_out, and_3_out);
  ExactlyOne xor_2 (.out(S1), .in0(A1), .in1(C0), .in2(B1));
  and and_4 (and_4_out, A1, B1);
  and and_5 (and_5_out, A1, C0);
  and and_6 (and_6_out, B1, C0);
  or or_2 (C1, and_4_out, and_5_out, and_6_out);
  ExactlyOne xor_3 (.out(S2), .in0(A2), .in1(C1), .in2(B2));
  and and_7 (and_7_out, A2, B2);
  and and_8 (and_8_out, A2, C1);
  and and_9 (and_9_out, B2, C1);
  or or_3 (C2, and_7_out, and_8_out, and_9_out);
  ExactlyOne xor_4 (.out(S3), .in0(A3), .in1(C2), .in2(B3));
  and and_10 (and_10_out, A3, B3);
  and and_11 (and_11_out, A3, C2);
  and and_12 (and_12_out, B3, C2);
  or or_4 (C3, and_10_out, and_11_out, and_12_out);
  ExactlyOne xor_5 (.out(S4), .in0(A4), .in1(C3), .in2(B4));
  and and_13 (and_13_out, A4, B4);
  and and_14 (and_14_out, A4, C3);
  and and_15 (and_15_out, B4, C3);
  or or_5 (C4, and_13_out, and_14_out, and_15_out);
  ExactlyOne xor_6 (.out(S5), .in0(A5), .in1(C4), .in2(B5));
  and and_16 (and_16_out, A5, B5);
  and and_17 (and_17_out, A5, C4);
  and and_18 (and_18_out, B5, C4);
  or or_6 (C5, and_16_out, and_17_out, and_18_out);
  ExactlyOne xor_7 (.out(S6), .in0(A6), .in1(C5), .in2(B6));
  and and_19 (and_19_out, A6, B6);
  and and_20 (and_20_out, A6, C5);
  and and_21 (and_21_out, B6, C5);
  or or_7 (C6, and_19_out, and_20_out, and_21_out);
  ExactlyOne xor_8 (.out(S7), .in0(A7), .in1(C6), .in2(B7));
  and and_22 (and_22_out, A7, B7);
  and and_23 (and_23_out, A7, C6);
  and and_24 (and_24_out, B7, C6);
  or or_8 (C7, and_22_out, and_23_out, and_24_out);
  ExactlyOne xor_9 (.out(S8), .in0(A8), .in1(C7), .in2(B8));
  and and_25 (and_25_out, A8, B8);
  and and_26 (and_26_out, A8, C7);
  and and_27 (and_27_out, B8, C7);
  or or_9 (C8, and_25_out, and_26_out, and_27_out);
  ExactlyOne xor_10 (.out(S9), .in0(A9), .in1(C8), .in2(B9));
  and and_28 (and_28_out, A9, B9);
  and and_29 (and_29_out, A9, C8);
  and and_30 (and_30_out, B9, C8);
  or or_10 (C9, and_28_out, and_29_out, and_30_out);
  ExactlyOne xor_11 (.out(S10), .in0(A10), .in1(C9), .in2(B10));
  and and_31 (and_31_out, A10, B10);
  and and_32 (and_32_out, A10, C9);
  and and_33 (and_33_out, B10, C9);
  or or_11 (C10, and_31_out, and_32_out, and_33_out);
  ExactlyOne xor_12 (.out(S11), .in0(A11), .in1(C10), .in2(B11));
  and and_34 (and_34_out, A11, B11);
  and and_35 (and_35_out, A11, C10);
  and and_36 (and_36_out, B11, C10);
  or or_12 (C11, and_34_out, and_35_out, and_36_out);
  ExactlyOne xor_13 (.out(S12), .in0(A12), .in1(C11), .in2(B12));
  and and_37 (and_37_out, A12, B12);
  and and_38 (and_38_out, A12, C11);
  and and_39 (and_39_out, B12, C11);
  or or_13 (C12, and_37_out, and_38_out, and_39_out);
  ExactlyOne xor_14 (.out(S13), .in0(A13), .in1(C12), .in2(B13));
  and and_40 (and_40_out, A13, B13);
  and and_41 (and_41_out, A13, C12);
  and and_42 (and_42_out, B13, C12);
  or or_14 (C13, and_40_out, and_41_out, and_42_out);
  ExactlyOne xor_15 (.out(S14), .in0(A14), .in1(C13), .in2(B14));
  and and_43 (and_43_out, A14, B14);
  and and_44 (and_44_out, A14, C13);
  and and_45 (and_45_out, B14, C13);
  or or_15 (C14, and_43_out, and_44_out, and_45_out);
  ExactlyOne xor_16 (.out(S15), .in0(A15), .in1(C14), .in2(B15));
  and and_46 (and_46_out, A15, B15);
  and and_47 (and_47_out, A15, C14);
  and and_48 (and_48_out, B15, C14);
  or or_16 (C15, and_46_out, and_47_out, and_48_out);
endmodule
