// Logisim project ADDER 16B.circ as structural Verilog: 5 circuits, main circuit halfadder
module halfadder (
  input  A,
  input  B,
  output S,
  output CO
);

  xor xor_1 (S, A, B);
  and and_1 (CO, A, B);
endmodule

module fulladder (
  input  Ci,
  input  A,
  input  B,
  output S,
  output CO
);

  wire halfadder_1_co, halfadder_1_s, halfadder_2_co;

  halfadder halfadder_1 (.A(A), .B(B), .S(halfadder_1_s), .CO(halfadder_1_co));
  halfadder halfadder_2 (.A(Ci), .B(halfadder_1_s), .S(S), .CO(halfadder_2_co));
  or or_1 (CO, halfadder_2_co, halfadder_1_co);
endmodule

module adder_4b (
  input  C0,
  input  A0,
  input  B0,
  input  A1,
  input  B1,
  input  A2,
  input  B2,
  input  A3,
  input  B3,
  output S0,
  output S1,
  output S2,
  output S3,
  output C4
);

  wire fulladder_1_co, fulladder_2_co, fulladder_3_co;

  fulladder fulladder_1 (.Ci(C0), .A(A0), .B(B0), .S(S0), .CO(fulladder_1_co));
  fulladder fulladder_2 (.Ci(fulladder_1_co), .A(A1), .B(B1), .S(S1), .CO(fulladder_2_co));
  fulladder fulladder_3 (.Ci(fulladder_2_co), .A(A2), .B(B2), .S(S2), .CO(fulladder_3_co));
  fulladder fulladder_4 (.Ci(fulladder_3_co), .A(A3), .B(B3), .S(S3), .CO(C4));
endmodule

module adder_8b (
  input  C0,
  input  A0,
  input  B0,
  input  A1,
  input  B1,
  input  A2,
  input  B2,
  input  A3,
  input  B3,
  input  A4,
  input  B4,
  input  A5,
  input  B5,
  input  A6,
  input  B6,
  input  A7,
  input  B7,
  output S0,
  output S1,
  output S2,
  output S3,
  output S4,
  output S5,
  output S6,
  output S7,
  output C8
);

  wire adder_4b_1_c4;

  adder_4b adder_4b_1 (
    .C0(C0), .A0(A0), .B0(B0), .A1(A1), .B1(B1), .A2(A2), .B2(B2), .A3(A3), .B3(B3), .S0(S0), .S1(S1),
    .S2(S2), .S3(S3), .C4(adder_4b_1_c4));
  adder_4b adder_4b_2 (
    .C0(adder_4b_1_c4), .A0(A4), .B0(B4), .A1(A5), .B1(B5), .A2(A6), .B2(B6), .A3(A7), .B3(B7), .S0(S4),
    .S1(S5), .S2(S6), .S3(S7), .C4(C8));
endmodule

module ADDER_16B (
  input  C0,
  input  A0,
  input  B0,
  input  A1,
  input  B1,
  input  A2,
  input  B2,
  input  A3,
  input  B3,
  input  A4,
  input  B4,
  input  A5,
  input  B5,
  input  A6,
  input  B6,
  input  A7,
  input  B7,
  input  A8,
  input  B8,
  input  A9,
  input  B9,
  input  A10,
  input  B10,
  input  A11,
  input  B11,
  input  A12,
  input  B12,
  input  A13,
  input  B13,
  input  A14,
  input  B14,
  input  A15,
  input  B15,
  output S0,
  output S1,
  output S2,
  output S3,
  output S4,
  output S5,
  output S6,
  output S7,
  output S8,
  output S9,
  output S10,
  output S11,
  output S12,
  output S13,
  output S14,
  output S15,
  output C
);

  wire adder_8b_1_c8;

  adder_8b adder_8b_1 (
    .C0(C0), .A0(A0), .B0(B0), .A1(A1), .B1(B1), .A2(A2), .B2(B2), .A3(A3), .B3(B3), .A4(A4), .B4(B4),
    .A5(A5), .B5(B5), .A6(A6), .B6(B6), .A7(A7), .B7(B7), .S0(S0), .S1(S1), .S2(S2), .S3(S3), .S4(S4),
    .S5(S5), .S6(S6), .S7(S7), .C8(adder_8b_1_c8));
  adder_8b adder_8b_2 (
    .C0(adder_8b_1_c8), .A0(A8), .B0(B8), .A1(A9), .B1(B9), .A2(A10), .B2(B10), .A3(A11), .B3(B11), .A4(A12),
    .B4(B12), .A5(A13), .B5(B13), .A6(A14), .B6(B14), .A7(A15), .B7(B15), .S0(S8), .S1(S9), .S2(S10),
    .S3(S11), .S4(S12), .S5(S13), .S6(S14), .S7(S15), .C8(C));
endmodule
