// Logisim project PARTE_1_ULA.circ as structural Verilog
module HALFADDER (
  input  A,
  input  B,
  output S,
  output C0
);

  xor xor_1 (S, A, B);
  and and_1 (C0, A, B);
endmodule

module FULLADDER (
  input  Ci,
  input  A,
  input  B,
  output S,
  output Co
);

  wire halfadder_1_c0, halfadder_1_s, halfadder_2_c0;

  HALFADDER halfadder_1 (.A(A), .B(B), .S(halfadder_1_s), .C0(halfadder_1_c0));
  HALFADDER halfadder_2 (.A(Ci), .B(halfadder_1_s), .S(S), .C0(halfadder_2_c0));
  or or_1 (Co, halfadder_2_c0, halfadder_1_c0);
endmodule

module ADDER_4b (
  input  Ci,
  input  A0,
  input  B0,
  input  A1,
  input  B1,
  input  A2,
  input  B2,
  input  A3,
  input  B3,
  output S0,
  output S1,
  output S2,
  output S3,
  output Co
);

  wire fulladder_1_co, fulladder_2_co, fulladder_3_co;

  FULLADDER fulladder_1 (.Ci(Ci), .A(A0), .B(B0), .S(S0), .Co(fulladder_1_co));
  FULLADDER fulladder_2 (.Ci(fulladder_1_co), .A(A1), .B(B1), .S(S1), .Co(fulladder_2_co));
  FULLADDER fulladder_3 (.Ci(fulladder_2_co), .A(A2), .B(B2), .S(S2), .Co(fulladder_3_co));
  FULLADDER fulladder_4 (.Ci(fulladder_3_co), .A(A3), .B(B3), .S(S3), .Co(Co));
endmodule

module ADDER_8b (
  input  Ci,
  input  A0,
  input  B0,
  input  A1,
  input  B1,
  input  A2,
  input  B2,
  input  A3,
  input  B3,
  input  A4,
  input  B4,
  input  A5,
  input  B5,
  input  A6,
  input  B6,
  input  A7,
  input  B7,
  output S0,
  output S1,
  output S2,
  output S3,
  output S4,
  output S5,
  output S6,
  output S7,
  output Co
);

  wire adder_4b_1_co;

  ADDER_4b adder_4b_1 (
    .Ci(Ci), .A0(A0), .B0(B0), .A1(A1), .B1(B1), .A2(A2), .B2(B2), .A3(A3), .B3(B3), .S0(S0), .S1(S1),
    .S2(S2), .S3(S3), .Co(adder_4b_1_co));
  ADDER_4b adder_4b_2 (
    .Ci(adder_4b_1_co), .A0(A4), .B0(B4), .A1(A5), .B1(B5), .A2(A6), .B2(B6), .A3(A7), .B3(B7), .S0(S4),
    .S1(S5), .S2(S6), .S3(S7), .Co(Co));
endmodule

module HALFSUB (
  input  A,
  input  B,
  output S,
  output Bout
);

  wire not_1_out;

  not not_1 (not_1_out, A);
  xor xor_1 (S, A, B);
  and and_1 (Bout, not_1_out, B);
endmodule

module FULLSUB (
  input  Bin,
  input  A,
  input  B,
  output S,
  output Bout
);

  wire halfsub_1_bout, halfsub_1_s, halfsub_2_bout;

  HALFSUB halfsub_1 (.A(A), .B(B), .S(halfsub_1_s), .Bout(halfsub_1_bout));
  HALFSUB halfsub_2 (.A(halfsub_1_s), .B(Bin), .S(S), .Bout(halfsub_2_bout));
  or or_1 (Bout, halfsub_2_bout, halfsub_1_bout);
endmodule

module SUB_4b (
  input  Ci,
  input  A0,
  input  B0,
  input  A1,
  input  B1,
  input  A2,
  input  B2,
  input  A3,
  input  B3,
  output S0,
  output S1,
  output S2,
  output S3,
  output Co
);

  wire fullsub_1_bout, fullsub_2_bout, fullsub_3_bout;

  FULLSUB fullsub_1 (.Bin(Ci), .A(A0), .B(B0), .S(S0), .Bout(fullsub_1_bout));
  FULLSUB fullsub_2 (.Bin(fullsub_1_bout), .A(A1), .B(B1), .S(S1), .Bout(fullsub_2_bout));
  FULLSUB fullsub_3 (.Bin(fullsub_2_bout), .A(A2), .B(B2), .S(S2), .Bout(fullsub_3_bout));
  FULLSUB fullsub_4 (.Bin(fullsub_3_bout), .A(A3), .B(B3), .S(S3), .Bout(Co));
endmodule

module SUB_8b (
  input  Ci,
  input  A0,
  input  B0,
  input  A1,
  input  B1,
  input  A2,
  input  B2,
  input  A3,
  input  B3,
  input  A4,
  input  B4,
  input  A5,
  input  B5,
  input  A6,
  input  B6,
  input  A7,
  input  B7,
  output S0,
  output S1,
  output S2,
  output S3,
  output S4,
  output S5,
  output S6,
  output S7,
  output Co
);

  wire sub_4b_1_co;

  SUB_4b sub_4b_1 (
    .Ci(Ci), .A0(A0), .B0(B0), .A1(A1), .B1(B1), .A2(A2), .B2(B2), .A3(A3), .B3(B3), .S0(S0), .S1(S1),
    .S2(S2), .S3(S3), .Co(sub_4b_1_co));
  SUB_4b sub_4b_2 (
    .Ci(sub_4b_1_co), .A0(A4), .B0(B4), .A1(A5), .B1(B5), .A2(A6), .B2(B6), .A3(A7), .B3(B7), .S0(S4),
    .S1(S5), .S2(S6), .S3(S7), .Co(Co));
endmodule

module MUX_8x1 (
  input  s0,
  input  s1,
  input  s2,
  input  Sum,
  input  Sub,
  input  Pin_and,
  input  Pin_Or,
  input  Pin_Xor,
  input  Pin_Nand,
  input  Pin_Nor,
  input  Pin_Xnor,
  output F
);

  wire and_1_out, and_2_out, and_3_out, and_4_out, and_5_out, and_6_out, and_7_out, and_8_out, and_9_out,
       and_10_out, and_11_out, and_12_out, and_13_out, and_14_out, and_15_out, and_16_out, or_1_out, or_2_out;

  and and_1 (and_1_out, ~s0, ~s1, ~s2);  // AND_Gate
  and and_2 (and_2_out, ~s2, ~s1, s0);  // AND_Gate
  and and_3 (and_3_out, ~s0, s1, ~s2);  // AND_Gate
  and and_4 (and_4_out, ~s2, s1, s0);  // AND_Gate
  and and_5 (and_5_out, s2, ~s1, ~s0);  // AND_Gate
  and and_6 (and_6_out, s2, ~s1, s0);  // AND_Gate
  and and_7 (and_7_out, s2, s1, ~s0);  // AND_Gate
  and and_8 (and_8_out, s0, s1, s2);
  and and_9 (and_9_out, and_1_out, Sum);
  and and_10 (and_10_out, and_2_out, Sub);
  and and_11 (and_11_out, and_3_out, Pin_and);
  and and_12 (and_12_out, and_4_out, Pin_Or);
  and and_13 (and_13_out, and_5_out, Pin_Xor);
  and and_14 (and_14_out, and_6_out, Pin_Nand);
  and and_15 (and_15_out, and_7_out, Pin_Nor);
  and and_16 (and_16_out, and_8_out, Pin_Xnor);
  or or_1 (or_1_out, and_9_out, and_10_out, and_11_out, and_12_out);
  or or_2 (or_2_out, and_13_out, and_14_out, and_15_out, and_16_out);
  or or_3 (F, or_1_out, or_2_out);
endmodule

module AND_8b (
  input  a0,
  input  b0,
  input  a1,
  input  b1,
  input  a2,
  input  b2,
  input  a3,
  input  b3,
  input  a4,
  input  b4,
  input  a5,
  input  b5,
  input  a6,
  input  b6,
  input  a7,
  input  b7,
  output s0,
  output s1,
  output s2,
  output s3,
  output s4,
  output s5,
  output s6,
  output s7
);

  and and_1 (s0, a0, b0);
  and and_2 (s1, a1, b1);
  and and_3 (s2, a2, b2);
  and and_4 (s3, a3, b3);
  and and_5 (s4, a4, b4);
  and and_6 (s5, a5, b5);
  and and_7 (s6, a6, b6);
  and and_8 (s7, a7, b7);
endmodule

module OR_8b (
  input  a0,
  input  b0,
  input  a1,
  input  b1,
  input  a2,
  input  b2,
  input  a3,
  input  b3,
  input  a4,
  input  b4,
  input  a5,
  input  b5,
  input  a6,
  input  b6,
  input  a7,
  input  b7,
  output s0,
  output s1,
  output s2,
  output s3,
  output s4,
  output s5,
  output s6,
  output s7
);

  or or_1 (s0, a0, b0);
  or or_2 (s1, a1, b1);
  or or_3 (s2, a2, b2);
  or or_4 (s3, a3, b3);
  or or_5 (s4, a4, b4);
  or or_6 (s5, a5, b5);
  or or_7 (s6, a6, b6);
  or or_8 (s7, a7, b7);
endmodule

module XOR_8b (
  input  a0,
  input  b0,
  input  a1,
  input  b1,
  input  a2,
  input  b2,
  input  a3,
  input  b3,
  input  a4,
  input  b4,
  input  a5,
  input  b5,
  input  a6,
  input  b6,
  input  a7,
  input  b7,
  output s0,
  output s1,
  output s2,
  output s3,
  output s4,
  output s5,
  output s6,
  output s7
);

  xor xor_1 (s0, a0, b0);
  xor xor_2 (s1, a1, b1);
  xor xor_3 (s2, a2, b2);
  xor xor_4 (s3, a3, b3);
  xor xor_5 (s4, a4, b4);
  xor xor_6 (s5, a5, b5);
  xor xor_7 (s6, a6, b6);
  xor xor_8 (s7, a7, b7);
endmodule

module NAND_8b (
  input  a0,
  input  b0,
  input  a1,
  input  b1,
  input  a2,
  input  b2,
  input  a3,
  input  b3,
  input  a4,
  input  b4,
  input  a5,
  input  b5,
  input  a6,
  input  b6,
  input  a7,
  input  b7,
  output s0,
  output s1,
  output s2,
  output s3,
  output s4,
  output s5,
  output s6,
  output s7
);

  nand nand_1 (s0, a0, b0);
  nand nand_2 (s1, a1, b1);
  nand nand_3 (s2, a2, b2);
  nand nand_4 (s3, a3, b3);
  nand nand_5 (s4, a4, b4);
  nand nand_6 (s5, a5, b5);
  nand nand_7 (s6, a6, b6);
  nand nand_8 (s7, a7, b7);
endmodule

module NOR_8b (
  input  a0,
  input  b0,
  input  a1,
  input  b1,
  input  a2,
  input  b2,
  input  a3,
  input  b3,
  input  a4,
  input  b4,
  input  a5,
  input  b5,
  input  a6,
  input  b6,
  input  a7,
  input  b7,
  output s0,
  output s1,
  output s2,
  output s3,
  output s4,
  output s5,
  output s6,
  output s7
);

  nor nor_1 (s0, a0, b0);
  nor nor_2 (s1, a1, b1);
  nor nor_3 (s2, a2, b2);
  nor nor_4 (s3, a3, b3);
  nor nor_5 (s4, a4, b4);
  nor nor_6 (s5, a5, b5);
  nor nor_7 (s6, a6, b6);
  nor nor_8 (s7, a7, b7);
endmodule

module XNOR_8b (
  input  a0,
  input  b0,
  input  a1,
  input  b1,
  input  a2,
  input  b2,
  input  a3,
  input  b3,
  input  a4,
  input  b4,
  input  a5,
  input  b5,
  input  a6,
  input  b6,
  input  a7,
  input  b7,
  output s0,
  output s1,
  output s2,
  output s3,
  output s4,
  output s5,
  output s6,
  output s7
);

  xnor xnor_1 (s0, a0, b0);
  xnor xnor_2 (s1, a1, b1);
  xnor xnor_3 (s2, a2, b2);
  xnor xnor_4 (s3, a3, b3);
  xnor xnor_5 (s4, a4, b4);
  xnor xnor_6 (s5, a5, b5);
  xnor xnor_7 (s6, a6, b6);
  xnor xnor_8 (s7, a7, b7);
endmodule

module ULA_1b (
  input  S2,
  input  S1,
  input  S0,
  input  Ci_sum,
  input  Ci_sub,
  input  A,
  input  B,
  output F,
  output Co_sum,
  output Co_sub
);

  wire fulladder_1_s, fullsub_1_s, ul_1_s_and, ul_1_s_nand, ul_1_s_nor, ul_1_s_or, ul_1_s_xnor, ul_1_s_xor;

  FULLADDER fulladder_1 (.Ci(Ci_sum), .A(A), .B(B), .S(fulladder_1_s), .Co(Co_sum));
  FULLSUB fullsub_1 (.Bin(Ci_sub), .A(A), .B(B), .S(fullsub_1_s), .Bout(Co_sub));
  UL ul_1 (
    .A(A), .B(B), .s_and(ul_1_s_and), .s_or(ul_1_s_or), .s_xor(ul_1_s_xor), .s_nand(ul_1_s_nand),
    .s_nor(ul_1_s_nor), .s_xnor(ul_1_s_xnor));
  MUX_8x1 mux_8x1_1 (
    .s0(S0), .s1(S1), .s2(S2), .Sum(fulladder_1_s), .Sub(fullsub_1_s), .Pin_and(ul_1_s_and),
    .Pin_Or(ul_1_s_or), .Pin_Xor(ul_1_s_xor), .Pin_Nand(ul_1_s_nand), .Pin_Nor(ul_1_s_nor),
    .Pin_Xnor(ul_1_s_xnor), .F(F));
endmodule

module UL (
  input  A,
  input  B,
  output s_and,
  output s_or,
  output s_xor,
  output s_nand,
  output s_nor,
  output s_xnor
);

  and and_1 (s_and, A, B);
  or or_1 (s_or, A, B);
  xor xor_1 (s_xor, A, B);
  nand nand_1 (s_nand, A, B);
  nor nor_1 (s_nor, A, B);
  xnor xnor_1 (s_xnor, A, B);
endmodule

module ULA_4B (
  input  S2,
  input  S1,
  input  S0,
  input  Ci_soma,
  input  Ci_subt,
  input  A0,
  input  B0,
  input  A1,
  input  B1,
  input  A2,
  input  B2,
  input  A3,
  input  B3,
  output F0,
  output F1,
  output F2,
  output F3,
  output C4_sum,
  output C4_sub
);

  wire ula_1b_1_co_sub, ula_1b_1_co_sum, ula_1b_2_co_sub, ula_1b_2_co_sum, ula_1b_3_co_sub, ula_1b_3_co_sum;

  ULA_1b ula_1b_1 (
    .S2(S2), .S1(S1), .S0(S0), .Ci_sum(Ci_soma), .Ci_sub(Ci_subt), .A(A0), .B(B0), .F(F0),
    .Co_sum(ula_1b_1_co_sum), .Co_sub(ula_1b_1_co_sub));
  ULA_1b ula_1b_2 (
    .S2(S2), .S1(S1), .S0(S0), .Ci_sum(ula_1b_1_co_sum), .Ci_sub(ula_1b_1_co_sub), .A(A1), .B(B1), .F(F1),
    .Co_sum(ula_1b_2_co_sum), .Co_sub(ula_1b_2_co_sub));
  ULA_1b ula_1b_3 (
    .S2(S2), .S1(S1), .S0(S0), .Ci_sum(ula_1b_2_co_sum), .Ci_sub(ula_1b_2_co_sub), .A(A2), .B(B2), .F(F2),
    .Co_sum(ula_1b_3_co_sum), .Co_sub(ula_1b_3_co_sub));
  ULA_1b ula_1b_4 (
    .S2(S2), .S1(S1), .S0(S0), .Ci_sum(ula_1b_3_co_sum), .Ci_sub(ula_1b_3_co_sub), .A(A3), .B(B3), .F(F3),
    .Co_sum(C4_sum), .Co_sub(C4_sub));
endmodule

module Sum_Sub (
  input  Sum_Ci,
  input  A,
  input  B,
  input  Min_Ci,
  output s_sum,
  output Co_sum,
  output s_sub,
  output Co_sub
);

  FULLADDER fulladder_1 (.Ci(Sum_Ci), .A(A), .B(B), .S(s_sum), .Co(Co_sum));
  FULLSUB fullsub_1 (.Bin(Min_Ci), .A(A), .B(B), .S(s_sub), .Bout(Co_sub));
endmodule

module ULA_8B (
  input  S2,
  input  S1,
  input  S0,
  input  Ci_sum,
  input  Ci_sub,
  input  A0,
  input  B0,
  input  A1,
  input  B1,
  input  A2,
  input  B2,
  input  A3,
  input  B3,
  input  A4,
  input  B4,
  input  A5,
  input  B5,
  input  A6,
  input  B6,
  input  A7,
  input  B7,
  output F7,
  output F5,
  output F3,
  output F1,
  output F0,
  output F6,
  output F4,
  output F2,
  output C8_sum,
  output C8_sub
);

  wire ula_4b_1_c4_sub, ula_4b_1_c4_sum;

  ULA_4B ula_4b_1 (
    .S2(S2), .S1(S1), .S0(S0), .Ci_soma(Ci_sum), .Ci_subt(Ci_sub), .A0(A0), .B0(B0), .A1(A1), .B1(B1),
    .A2(A2), .B2(B2), .A3(A3), .B3(B3), .F0(F0), .F1(F1), .F2(F2), .F3(F3), .C4_sum(ula_4b_1_c4_sum),
    .C4_sub(ula_4b_1_c4_sub));
  ULA_4B ula_4b_2 (
    .S2(S2), .S1(S1), .S0(S0), .Ci_soma(ula_4b_1_c4_sum), .Ci_subt(ula_4b_1_c4_sub), .A0(A4), .B0(B4),
    .A1(A5), .B1(B5), .A2(A6), .B2(B6), .A3(A7), .B3(B7), .F0(F4), .F1(F5), .F2(F6), .F3(F7),
    .C4_sum(C8_sum), .C4_sub(C8_sub));
endmodule
