// Logisim project ULA_8BITS.circ as structural Verilog: 9 circuits, main circuit Ula_8b
module HalfAdder (
  input  A,
  input  B,
  output S,
  output C0
);

  xor xor_1 (S, A, B);
  and and_1 (C0, A, B);
endmodule

module FullAdder (
  input  Ci,
  input  A,
  input  B,
  output S,
  output Co
);

  wire halfadder_1_c0, halfadder_1_s, halfadder_2_c0;

  HalfAdder halfadder_1 (.A(A), .B(B), .S(halfadder_1_s), .C0(halfadder_1_c0));
  HalfAdder halfadder_2 (.A(Ci), .B(halfadder_1_s), .S(S), .C0(halfadder_2_c0));
  or or_1 (Co, halfadder_2_c0, halfadder_1_c0);
endmodule

module HalfSub (
  input  A,
  input  B,
  output S,
  output Bout
);

  wire not_1_out;

  not not_1 (not_1_out, A);
  xor xor_1 (S, A, B);
  and and_1 (Bout, not_1_out, B);
endmodule

module FullSub (
  input  Bin,
  input  A,
  input  B,
  output S,
  output Bout
);

  wire halfsub_1_bout, halfsub_1_s, halfsub_2_bout;

  HalfSub halfsub_1 (.A(A), .B(B), .S(halfsub_1_s), .Bout(halfsub_1_bout));
  HalfSub halfsub_2 (.A(halfsub_1_s), .B(Bin), .S(S), .Bout(halfsub_2_bout));
  or or_1 (Bout, halfsub_2_bout, halfsub_1_bout);
endmodule

module Mux_8x1 (
  input  s0,
  input  s1,
  input  s2,
  input  Sum,
  input  Sub,
  input  Pin_and,
  input  Pin_Or,
  input  Pin_Xor,
  input  Pin_Nand,
  input  Pin_Nor,
  input  Pin_Xnor,
  output F
);

  wire and_1_out, and_2_out, and_3_out, and_4_out, and_5_out, and_6_out, and_7_out, and_8_out, and_9_out,
       and_10_out, and_11_out, and_12_out, and_13_out, and_14_out, and_15_out, and_16_out, or_1_out, or_2_out;

  and and_1 (and_1_out, ~s0, ~s1, ~s2);  // AND_Gate
  and and_2 (and_2_out, ~s2, ~s1, s0);  // AND_Gate
  and and_3 (and_3_out, ~s0, s1, ~s2);  // AND_Gate
  and and_4 (and_4_out, ~s2, s1, s0);  // AND_Gate
  and and_5 (and_5_out, s2, ~s1, ~s0);  // AND_Gate
  and and_6 (and_6_out, s2, ~s1, s0);  // AND_Gate
  and and_7 (and_7_out, s2, s1, ~s0);  // AND_Gate
  and and_8 (and_8_out, s0, s1, s2);
  and and_9 (and_9_out, and_1_out, Sum);
  and and_10 (and_10_out, and_2_out, Sub);
  and and_11 (and_11_out, and_3_out, Pin_and);
  and and_12 (and_12_out, and_4_out, Pin_Or);
  and and_13 (and_13_out, and_5_out, Pin_Xor);
  and and_14 (and_14_out, and_6_out, Pin_Nand);
  and and_15 (and_15_out, and_7_out, Pin_Nor);
  and and_16 (and_16_out, and_8_out, Pin_Xnor);
  or or_1 (or_1_out, and_9_out, and_10_out, and_11_out, and_12_out);
  or or_2 (or_2_out, and_13_out, and_14_out, and_15_out, and_16_out);
  or or_3 (F, or_1_out, or_2_out);
endmodule

module Ula_1b (
  input  S2,
  input  S1,
  input  S0,
  input  Ci_sum,
  input  Ci_sub,
  input  A,
  input  B,
  output F,
  output Co_sum,
  output Co_sub
);

  wire fulladder_1_s, fullsub_1_s, logic_ports_1_s_and, logic_ports_1_s_nand, logic_ports_1_s_nor,
       logic_ports_1_s_or, logic_ports_1_s_xnor, logic_ports_1_s_xor;

  FullAdder fulladder_1 (.Ci(Ci_sum), .A(A), .B(B), .S(fulladder_1_s), .Co(Co_sum));
  FullSub fullsub_1 (.Bin(Ci_sub), .A(A), .B(B), .S(fullsub_1_s), .Bout(Co_sub));
  Logic_ports logic_ports_1 (
    .A(A), .B(B), .s_and(logic_ports_1_s_and), .s_or(logic_ports_1_s_or), .s_xor(logic_ports_1_s_xor),
    .s_nand(logic_ports_1_s_nand), .s_nor(logic_ports_1_s_nor), .s_xnor(logic_ports_1_s_xnor));
  Mux_8x1 mux_8x1_1 (
    .s0(S0), .s1(S1), .s2(S2), .Sum(fulladder_1_s), .Sub(fullsub_1_s), .Pin_and(logic_ports_1_s_and),
    .Pin_Or(logic_ports_1_s_or), .Pin_Xor(logic_ports_1_s_xor), .Pin_Nand(logic_ports_1_s_nand),
    .Pin_Nor(logic_ports_1_s_nor), .Pin_Xnor(logic_ports_1_s_xnor), .F(F));
endmodule

module Logic_ports (
  input  A,
  input  B,
  output s_and,
  output s_or,
  output s_xor,
  output s_nand,
  output s_nor,
  output s_xnor
);

  and and_1 (s_and, A, B);
  or or_1 (s_or, A, B);
  xor xor_1 (s_xor, A, B);
  nand nand_1 (s_nand, A, B);
  nor nor_1 (s_nor, A, B);
  xnor xnor_1 (s_xnor, A, B);
endmodule

module Ula_4b (
  input  S2,
  input  S1,
  input  S0,
  input  Ci_soma,
  input  Ci_subt,
  input  A0,
  input  B0,
  input  A1,
  input  B1,
  input  A2,
  input  B2,
  input  A3,
  input  B3,
  output F0,
  output F1,
  output F2,
  output F3,
  output C4_sum,
  output C4_sub
);

  wire ula_1b_1_co_sub, ula_1b_1_co_sum, ula_1b_2_co_sub, ula_1b_2_co_sum, ula_1b_3_co_sub, ula_1b_3_co_sum;

  Ula_1b ula_1b_1 (
    .S2(S2), .S1(S1), .S0(S0), .Ci_sum(Ci_soma), .Ci_sub(Ci_subt), .A(A0), .B(B0), .F(F0),
    .Co_sum(ula_1b_1_co_sum), .Co_sub(ula_1b_1_co_sub));
  Ula_1b ula_1b_2 (
    .S2(S2), .S1(S1), .S0(S0), .Ci_sum(ula_1b_1_co_sum), .Ci_sub(ula_1b_1_co_sub), .A(A1), .B(B1), .F(F1),
    .Co_sum(ula_1b_2_co_sum), .Co_sub(ula_1b_2_co_sub));
  Ula_1b ula_1b_3 (
    .S2(S2), .S1(S1), .S0(S0), .Ci_sum(ula_1b_2_co_sum), .Ci_sub(ula_1b_2_co_sub), .A(A2), .B(B2), .F(F2),
    .Co_sum(ula_1b_3_co_sum), .Co_sub(ula_1b_3_co_sub));
  Ula_1b ula_1b_4 (
    .S2(S2), .S1(S1), .S0(S0), .Ci_sum(ula_1b_3_co_sum), .Ci_sub(ula_1b_3_co_sub), .A(A3), .B(B3), .F(F3),
    .Co_sum(C4_sum), .Co_sub(C4_sub));
endmodule

module Ula_8b (
  input  S2,
  input  S1,
  input  S0,
  input  Ci_sum,
  input  Ci_sub,
  input  A0,
  input  B0,
  input  A1,
  input  B1,
  input  A2,
  input  B2,
  input  A3,
  input  B3,
  input  A4,
  input  B4,
  input  A5,
  input  B5,
  input  A6,
  input  B6,
  input  A7,
  input  B7,
  output F7,
  output F5,
  output F3,
  output F1,
  output F0,
  output F6,
  output F4,
  output F2,
  output C8_sum,
  output C8_sub
);

  wire ula_4b_1_c4_sub, ula_4b_1_c4_sum;

  Ula_4b ula_4b_1 (
    .S2(S2), .S1(S1), .S0(S0), .Ci_soma(Ci_sum), .Ci_subt(Ci_sub), .A0(A0), .B0(B0), .A1(A1), .B1(B1),
    .A2(A2), .B2(B2), .A3(A3), .B3(B3), .F0(F0), .F1(F1), .F2(F2), .F3(F3), .C4_sum(ula_4b_1_c4_sum),
    .C4_sub(ula_4b_1_c4_sub));
  Ula_4b ula_4b_2 (
    .S2(S2), .S1(S1), .S0(S0), .Ci_soma(ula_4b_1_c4_sum), .Ci_subt(ula_4b_1_c4_sub), .A0(A4), .B0(B4),
    .A1(A5), .B1(B5), .A2(A6), .B2(B6), .A3(A7), .B3(B7), .F0(F4), .F1(F5), .F2(F6), .F3(F7),
    .C4_sum(C8_sum), .C4_sub(C8_sub));
endmodule
